# Fritzing sketch Circuit (saved by Fritzing 0.9.0b)
perfboards: 1

parts:
  J1 = female pin header, 8 pins [form="♀ (female)" part_number="Nokia 5110 Display"]
  Teensy1 = Teensy 3.0
  J2 = female pin header, 13 pins [form="♀ (female)"]
  J2_2 = female pin header, 13 pins [form="♀ (female)" part_number="Key Matrix"]
  J3 = female pin header, 13 pins [form="♀ (female)"]
  IC1 = IC, DIP package, 28 pins [chip_label=IC]
  R2 = Resistor [tolerance=±5% resistance=4.7k package=THT]
  R3 = Resistor [tolerance=±5% resistance=4.7k package=THT]
  IC2 = IC, DIP package, 8 pins [chip_label=IC]

nets:
  N1: J1.pin1, Teensy1.VBat, Teensy1.3V3#30, IC1.pin11, IC1.pin16, R2.Pin_0, R3.Pin_0, IC2.pin3, IC2.pin7, IC2.pin8
  N2: J1.pin2, Teensy1.GND, IC1.pin1, IC1.pin15, IC2.pin4
  N3: J1.pin3, Teensy1.A2/D16
  N4: J1.pin4, Teensy1.A1/D15
  N5: J1.pin5, Teensy1.A0/D14
  N6: J1.pin6, Teensy1.D11, IC2.pin5
  N7: J1.pin7, J1.pin8, Teensy1.D13, IC2.pin6
  N8: Teensy1.D0, J2.pin1, J2_2.pin1
  N9: Teensy1.D1, J2.pin2, J2_2.pin2
  N10: Teensy1.D2, J2.pin3, J2_2.pin3
  N11: Teensy1.D3, J2.pin4, J2_2.pin4
  N12: Teensy1.D4, J2.pin5, J2_2.pin5
  N13: Teensy1.D5, J2.pin6, J2_2.pin6
  N14: Teensy1.D6, J2.pin7, J2_2.pin7
  N15: Teensy1.D7, J2.pin8, J2_2.pin8
  N16: Teensy1.D8, J2.pin9, J2_2.pin9
  N17: Teensy1.D9, J2.pin10, J2_2.pin10
  N18: Teensy1.D10, J2.pin11, J2_2.pin11
  N19: Teensy1.D12, IC2.pin2
  N20: Teensy1.A3/D17, J2.pin13, J2_2.pin13
  N21: Teensy1.A4/D18, IC1.pin13, R3.Pin_1
  N22: Teensy1.A5/D19, IC1.pin12, R2.Pin_1
  N23: Teensy1.A6/D20, J2.pin12, J2_2.pin12
  N24: Teensy1.A7/D21, IC2.pin1
  N25: J3.pin1, IC1.pin3
  N26: J3.pin2, IC1.pin4
  N27: J3.pin3, IC1.pin5
  N28: J3.pin4, IC1.pin6
  N29: J3.pin5, IC1.pin7
  N30: J3.pin6, IC1.pin8
  N31: J3.pin7, IC1.pin27
  N32: J3.pin8, IC1.pin26
  N33: J3.pin9, IC1.pin25
  N34: J3.pin10, IC1.pin24
  N35: J3.pin11, IC1.pin23
  N36: J3.pin12, IC1.pin22
  N37: J3.pin13, IC1.pin21

notes:
  Nokia 5110
